// Digital circuit Register_file.dig as structural Verilog
module Register_file (
  input  [1:0] Select_read1,
  input  [1:0] Select_read2,
  input  clk,
  input  [3:0] Write_Data,
  input  [1:0] Select_write,
  input  [7:0] CTRL_registers,
  output [3:0] Read_Data_1,
  output [3:0] Read_Data_2
);

  wire [3:0] demultiplexer_1_out_0, demultiplexer_1_out_1, demultiplexer_1_out_2, demultiplexer_1_out_3,
       R_0_p4, R_1_p4, R_2_p4, R_3_p4;

  Demultiplexer #(.Bits(4), .Selector_Bits(2)) demultiplexer_1 (
    .sel(Select_write), .in(Write_Data), .out_0(demultiplexer_1_out_0), .out_1(demultiplexer_1_out_1),
    .out_2(demultiplexer_1_out_2), .out_3(demultiplexer_1_out_3));
  // _4bitregister R_0: pin names not known; wires that end beside it: clk, demultiplexer_1_out_0, CTRL_registers[1:0], R_0_p4
  // _4bitregister R_1: pin names not known; wires that end beside it: clk, demultiplexer_1_out_1, CTRL_registers[3:2], R_1_p4
  // _4bitregister R_2: pin names not known; wires that end beside it: clk, demultiplexer_1_out_2, CTRL_registers[5:4], R_2_p4
  // _4bitregister R_3: pin names not known; wires that end beside it: clk, demultiplexer_1_out_3, CTRL_registers[7:6], R_3_p4
  Multiplexer #(.Bits(4), .Selector_Bits(2)) multiplexer_1 (
    .sel(Select_read1), .in_0(R_0_p4), .in_1(R_1_p4), .in_2(R_2_p4), .in_3(R_3_p4), .out(Read_Data_1));
  Multiplexer #(.Selector_Bits(2), .Bits(4)) multiplexer_2 (
    .sel(Select_read2), .in_0(R_0_p4), .in_1(R_1_p4), .in_2(R_2_p4), .in_3(R_3_p4), .out(Read_Data_2));
endmodule
